// Logisim project cpu.circ as structural Verilog: 1 circuit, main circuit main
module main (
  input  [31:0] INSTRUCTION,
  input  CLOCK,
  output [31:0] FETCH_ADDRESS,
  output [31:0] s0_Value,
  output [31:0] s1_Value,
  output [31:0] t0_Value,
  output [31:0] t1_Value,
  output [31:0] a0_Value,
  output [31:0] ra_Value,
  output [31:0] sp_Value
);

  wire main_1_p1, main_1_p2, main_1_p4, main_2_p1, MEM_p1, MEM_p4, MEM_p7, MEM_p10;

  Register #(.width(16)) PC ();  // open: D, en, Q, clk, clr
  // regfile_main main_1: pin names not known; wires that end beside it: main_1_p1, main_1_p2, main_1_p2, main_1_p4
  // alu_main main_2: pin names not known; wires that end beside it: main_2_p1, s0_Value
  // mem_main MEM: pin names not known; wires that end beside it: MEM_p1, MEM_p1, s1_Value, MEM_p4, MEM_p4, t0_Value, MEM_p7, MEM_p7, t1_Value, MEM_p10, MEM_p10, a0_Value

  // Other names for the same wires on the sheet: clk = CLOCK; fetch_addr[31:0] = FETCH_ADDRESS

  // Notes on the sheet:
  //   Output
  //   These are outputs/inputs from run.circ
  //   Inputs
  //   These are DEBUG/TEST outputs from your circuit.
endmodule
